# Fritzing sketch controleFESrowing (saved by Fritzing 0.9.3b)
circuit board: 8.19789cm x 5.32283cm

parts:
  Componente1 = Arduino Pro Mini v13
  Componente2 = Bluetooth HC-05 Macho
  S1 = Round Pushbutton
  S6 = Round Pushbutton
  S7 = Round Pushbutton
  VCC1 = Battery block 9V
  R2 = Resistor [tolerance=±5% resistance=220 package="2512 [SMD]"]
  R1 = Resistor [tolerance=±5% resistance=220 package="2512 [SMD]"]
  U1 = LCD-16X2 [package=lcd-16x2]

nets:
  VCC: Componente1.VCC, Componente2.VCC, U1.VDD, U1.A
  N1: Componente1.RAW, VCC1.+
  GND: Componente1.GND, Componente2.GND, S1.leg0, S6.leg0, S7.leg0, VCC1.-, R2.Pin_0, U1.VSS, U1.VO, U1.R_W, U1.K
  N2: Componente1.D12/MISO, U1.RS
  N3: Componente1.D11_PWM/MOSI, U1.E
  N4: Componente1.D10_PWM/SS, Componente2.RXD
  N5: Componente1.D9_PWM, R1.Pin_1
  N6: Componente1.D8, S7.leg1
  N7: Componente1.D7, S6.leg1
  N8: Componente1.D6_PWM, S1.leg1
  N9: Componente1.D5_PWM, U1.DB4
  N10: Componente1.D4, U1.DB5
  N11: Componente1.D3_PWM, U1.DB6
  N12: Componente1.D2, U1.DB7
  N13: Componente2.TXD, R2.Pin_1, R1.Pin_0
